# Fritzing sketch poseur-blocks-schematic (saved by Fritzing 0.8.7b)
breadboards: 1

parts:
  Part1 = Arduino Uno (Rev3)
  LCD1 = LCD screen
  J1 = Piezo Speaker
  R1 = Resistor [tolerance=±5% resistance=10k package=THT]
  R2 = Resistor [tolerance=±5% resistance=220 package=THT]
  S1 = Pushbutton [package="[THT]"]
  S2 = Pushbutton [package="[THT]"]
  S3 = Pushbutton [package="[THT]"]
  R3 = Resistor [tolerance=±5% resistance=10k package=THT]
  R4 = Resistor [tolerance=±5% resistance=220 package=THT]
  R4_2 = Trimmer Potentiometer [maximum_resistance=100kΩ package=THT]

nets:
  N1: Part1.A0, S1.Pin_2, S2.Pin_2, S3.Pin_2, R3.Pin_0
  N2: Part1.D8, J1.pin1
  N3: Part1.D11_PWM/MOSI, LCD1.E
  N4: Part1.D12/MISO, LCD1.RS
  N5: Part1.D2, LCD1.DB7
  N6: Part1.D3_PWM, LCD1.DB6
  N7: Part1.D4, LCD1.DB5
  N8: Part1.D5_PWM, LCD1.DB4
  5V: Part1.5V, LCD1.VDD, R1.Pin_0, R2.Pin_0, S3.Pin_4, R4.Pin_0, R4_2.leg2
  GND: Part1.GND, LCD1.VSS, LCD1.LED-, J1.pin2, R3.Pin_1, R4_2.leg1
  N9: LCD1.V0, R4_2.wiper
  N10: LCD1.LED+, R4.Pin_1
  N11: R1.Pin_1, S1.Pin_4
  N12: R2.Pin_1, S2.Pin_3, S2.Pin_4
